# Fritzing sketch TitoPlayer (saved by Fritzing 0.9.3b)

parts:
  MCU1 = Raspberry Pi Zero
  Part2 = Adafruit MAX98357A I2S 3W Class D Amplifier [part_number="Adafruit #3006"]
  BAT1 = Battery Holders [package=lipo-1100mAh]
  SP1 = SPEAKER [package=pcb_mount_speaker]
  Part3 = PowerBoost 1000 Basic
  S2 = Momentary Switch [package=ksa_sealed_tac_switch]
  S3 = Momentary Switch [package=ksa_sealed_tac_switch]
  S4 = Momentary Switch [package=ksa_sealed_tac_switch]
  S5 = Momentary Switch [package=ksa_sealed_tac_switch]
  S6 = Momentary Switch [package=ksa_sealed_tac_switch]
  S7 = Momentary Switch [package=ksa_sealed_tac_switch]
  U1 = 3.5mm Audio Jack [package=audio-jack-3.5mm-smd]
  U2 = RELAY [package=OJ]
  S8 = SWITCH-SP3T [package=switch-sp3t-smd]
  J1 = female pin header, 7 pins [form="♀ (female)"]

nets:
  N1: MCU1.pin_2, MCU1.pin_4, Part2.VIN, Part3.5.0V
  GND: MCU1.pin_6, MCU1.pin_9, MCU1.pin_20, MCU1.pin_30, MCU1.pin_34, MCU1.pin_39, Part2.GND, BAT1.-, Part3.GND, S6.2, U2.COIL2, J1.pin7
  N2: MCU1.pin_7, S8.4
  N3: MCU1.pin_11, S2.1
  N4: MCU1.pin_12, Part2.BCLK
  N5: MCU1.pin_13, S4.1
  N6: MCU1.pin_15, S5.1
  N7: MCU1.pin_18, U2.COIL1
  N8: MCU1.pin_29, S7.2
  N9: MCU1.pin_31, S3.1
  N10: MCU1.pin_35, Part2.LRCLK
  N11: MCU1.pin_40, Part2.DIN
  N12: Part2.VO-, SP1.+, U1.SLEEVE
  N13: Part2.VO+, U1.RIGHT, U1.LEFT, U2.MAIN
  N14: BAT1.+, Part3.VBAT
  N15: SP1.-, U2.NO
  N16: Part3.ENABLE, S6.1
  N17: S2.2, J1.pin3
  N18: S3.2, J1.pin6
  N19: S4.2, J1.pin4
  N20: S5.2, J1.pin5
  N21: S7.3, J1.pin2
  N22: S8.3, J1.pin1

notes:
  5V USB Charger
  POWER
  PLAY
  FF
  SPEKER
  STOP/
  REW
  EJECT
  ENABLE
  GND
  Reset
  WIFI

custom parts:
  Adafruit MAX98357A I2S 3W Class D Amplifier: Listen to this good news - we now have an all in one digital audio amp breakout board that works incredibly well with the Raspberry Pi! If you're looking for an easy and low cost way to get you digital sound files bumpin' then the MAX08357 I2S Amp Breakout is for you. It takes standard I2S digital audio input and, not only decodes it into analog, but also amplifies it directly into a speaker.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
  PowerBoost 1000 Basic: The PowerBoost 1000 is a little DC/DC boost converter module that can run from 1.8V batteries or higher, and convert the battery output to 5.2V DC for running your 5V projects. At its heart is a TPS61030 boost converter from TI. This boost converter chip has some really nice extras such as low battery detection, 4A internal switch, synchronous conversion, excellent efficiency, and 700KHz high-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
